# Fritzing sketch module2 (saved by Fritzing 1.0.3b)
breadboards: 1

parts:
  Mod1 = ESP32-TTGO-T-DISPLAY
  Part1 = Black Joystick KY-023
  R1 = 6mm Trimmer Potentiometer [maximum_resistance=10kΩ knob_status=50% power=0.5W package=THT]
  S1 = Pushbutton [package="[SMD]"]

nets:
  N1: Mod1.G-1, Mod1.G-2, Mod1.G-10, Mod1.G-11, Mod1.G-14, Part1.GND, R1.leg1, S1.Pin_1, S1.Pin_2
  N2: Mod1.2, R1.wiper
  N3: Mod1.12, S1.Pin_3, S1.Pin_4
  N4: Mod1.3V, Part1.+5V, R1.leg2
  N5: Mod1.32, Part1.SW
  N6: Mod1.39, Part1.VRy
  N7: Mod1.38, Part1.VRx

custom parts:
  ESP32-TTGO-T-DISPLAY: LILYGO TTGO T-Display GD32VF103CBT6 Main Chip ST7789 1.14 Inch IPS 240x135 Resolution Minimalist Development Board.
  Black Joystick KY-023: Description: The joystick is a combination of 2 analoog potentiometer and a digital switch. Arduino GND --> Module pin - Arduino +5V --> Module pin +5V Arduino Analoog 0 --> Module VRx Arduino Analoog 1 --> Module VRy Arduino Digital --> Module SW Dimensions: 1" x 1.25"
